# Fritzing sketch OpenSpool (saved by Fritzing 1.0.4)

parts:
  Part1 = PN532 Elechouse RFID NFC Module V3
  A1 = Wemos S2 Mini [part_number="WeMos D1 Mini Lite"]
  Part2 = PN532 Elechouse RFID NFC Module V3
  A2 = Wemos S2 Mini [part_number="WeMos D1 Mini Lite"]
  Part3 = PN532 Elechouse RFID NFC Module V3

nets:
  N1: Part1.SCK, A1.Pin_30
  N2: Part1.MISO, A1.Pin_23
  N3: Part1.MOSI, A1.Pin_22
  N4: Part1.SS, A1.Pin_29
  VCC: Part1.VCC, A1.Pin_17, Part3.VCC
  GND: Part1.GND, A1.Pin_18, A1.Pin_26, Part3.GND
  N5: A1.Pin_1, Part3.SCL
  N6: A1.Pin_2, Part3.SDA
  N7: Part2.SCK, A2.Pin_30
  N8: Part2.MISO, A2.Pin_23
  N9: Part2.MOSI, A2.Pin_22
  N10: Part2.SS, A2.Pin_29
  N11: Part2.VCC, A2.Pin_17
  N12: Part2.GND, A2.Pin_18, A2.Pin_26

custom parts:
  PN532 Elechouse RFID NFC Module V3: NFC is a popular technology in recent years. We often heard this work while smart phone company such as Samsung or HTC introduces their latest high-end phones. Almost all the high-end phone in the market support NFC. Near field communication (NFC) is a set of standards for smart phones and similar devices to establish radio communication with each other by touching them together or bringing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
  Wemos S2 Mini: A mini wifi board based on the ESP32-S2FN4R2.
